// Logisim project CPU_Library.circ as structural Verilog
module AND (
  input  [5:0] A5_A0,
  input  [5:0] B5_B0,
  output [5:0] out_3
);

  and _0 (out_3[0], A5_A0[0], B5_B0[0]);
  and _1 (out_3[1], A5_A0[1], B5_B0[1]);
  and _2 (out_3[2], A5_A0[2], B5_B0[2]);
  and _3 (out_3[3], A5_A0[3], B5_B0[3]);
  and _4 (out_3[4], A5_A0[4], B5_B0[4]);
  and _5 (out_3[5], A5_A0[5], B5_B0[5]);

  // Other names for the same wires on the sheet: A0 = A5_A0[0]; A1 = A5_A0[1]; A2 = A5_A0[2]; A3 = A5_A0[3];
  //   A4 = A5_A0[4]; A5 = A5_A0[5]; B0 = B5_B0[0]; B1 = B5_B0[1]; B2 = B5_B0[2]; B3 = B5_B0[3]; B4 = B5_B0[4];
  //   B5 = B5_B0[5]; R0 = out_3[0]; R1 = out_3[1]; R2 = out_3[2]; R3 = out_3[3]; R4 = out_3[4]; R5 = out_3[5]
endmodule

module ROR (
  input  [5:0] A5_A0,
  input  [2:0] Shift_2_0,
  output [5:0] out_3
);

  Multiplexer #(.select(3), .enable("false")) multiplexer_1 (
    .in0(A5_A0[5]), .in1(A5_A0[0]), .in2(A5_A0[1]), .in3(A5_A0[2]), .in4(A5_A0[3]), .in5(A5_A0[4]),
    .in6(1'b0), .in7(1'b0), .out(out_3[5]), .sel(Shift_2_0));
  Multiplexer #(.select(3), .enable("false")) multiplexer_2 (
    .in0(A5_A0[4]), .in1(A5_A0[5]), .in2(A5_A0[0]), .in3(A5_A0[1]), .in4(A5_A0[2]), .in5(A5_A0[3]),
    .in6(1'b0), .in7(1'b0), .out(out_3[4]), .sel(Shift_2_0));
  Multiplexer #(.select(3), .enable("false")) multiplexer_3 (
    .in0(A5_A0[3]), .in1(A5_A0[4]), .in2(A5_A0[5]), .in3(A5_A0[0]), .in4(A5_A0[1]), .in5(A5_A0[2]),
    .in6(1'b0), .in7(1'b0), .out(out_3[3]), .sel(Shift_2_0));
  Multiplexer #(.select(3), .enable("false")) multiplexer_4 (
    .in0(A5_A0[2]), .in1(A5_A0[3]), .in2(A5_A0[4]), .in3(A5_A0[5]), .in4(A5_A0[0]), .in5(A5_A0[1]),
    .in6(1'b0), .in7(1'b0), .out(out_3[2]), .sel(Shift_2_0));
  Multiplexer #(.select(3), .enable("false")) multiplexer_5 (
    .in0(A5_A0[1]), .in1(A5_A0[2]), .in2(A5_A0[3]), .in3(A5_A0[4]), .in4(A5_A0[5]), .in5(A5_A0[0]),
    .in6(1'b0), .in7(1'b0), .out(out_3[1]), .sel(Shift_2_0));
  Multiplexer #(.select(3), .enable("false")) multiplexer_6 (
    .in0(A5_A0[0]), .in1(A5_A0[1]), .in2(A5_A0[2]), .in3(A5_A0[3]), .in4(A5_A0[4]), .in5(A5_A0[5]),
    .in6(1'b0), .in7(1'b0), .out(out_3[0]), .sel(Shift_2_0));

  // Other names for the same wires on the sheet: A0 = A5_A0[0]; A1 = A5_A0[1]; A2 = A5_A0[2]; A3 = A5_A0[3];
  //   A4 = A5_A0[4]; A5 = A5_A0[5]; R0 = out_3[0]; R1 = out_3[1]; R2 = out_3[2]; R3 = out_3[3]; R4 = out_3[4];
  //   R5 = out_3[5]
endmodule

module ALU (
  input  [5:0] A_5_0,
  input  [5:0] B_5_0,
  input  [2:0] Shift_2_0,
  input  [3:0] OP,
  output [5:0] out_5,
  output SF,
  output CF,
  output ZF
);

  wire or_1_out;
  wire [5:0] and_1_out_3, ror_1_out_3;

  AND and_1 (.A5_A0(A_5_0), .B5_B0(B_5_0), .out_3(and_1_out_3));
  ROR ror_1 (.A5_A0(A_5_0), .Shift_2_0(Shift_2_0), .out_3(ror_1_out_3));
  Multiplexer #(.select(4), .width(6), .enable("false")) multiplexer_1 (
    .in0(and_1_out_3), .in1(ror_1_out_3), .out(out_5), .sel(OP));  // open: in2, in3, in4, in5, in6, in7, in8, in9, in10, in11, in12, in13, in14, in15
  or or_1 (or_1_out, out_5[0], out_5[1], out_5[2], out_5[3], out_5[4], out_5[5]);
  not not_1 (ZF, or_1_out);

  assign CF = 1'b0;
  assign SF = out_5[5];
endmodule

module _1_bit_register (
  input  Din,
  input  Sel,
  input  Clk,
  output Dout
);

  wire multiplexer_1_out;

  Multiplexer #(.enable("false")) multiplexer_1 (.in0(Dout), .in1(Din), .out(multiplexer_1_out), .sel(Sel));
  D_Flip_Flop d_ff_1 (.clk(Clk), .D(multiplexer_1_out), .Q(Dout));  // open: Qn, preset, en, reset
endmodule

module _6_bit_register (
  input  [5:0] Din_5_0,
  input  Dsel,
  input  Clk,
  output [5:0] out_4
);

  _1_bit_register u_1_bit_register_1 (.Din(Din_5_0[0]), .Sel(Dsel), .Clk(Clk), .Dout(out_4[0]));
  _1_bit_register u_1_bit_register_2 (.Din(Din_5_0[1]), .Sel(Dsel), .Clk(Clk), .Dout(out_4[1]));
  _1_bit_register u_1_bit_register_3 (.Din(Din_5_0[2]), .Sel(Dsel), .Clk(Clk), .Dout(out_4[2]));
  _1_bit_register u_1_bit_register_4 (.Din(Din_5_0[3]), .Sel(Dsel), .Clk(Clk), .Dout(out_4[3]));
  _1_bit_register u_1_bit_register_5 (.Din(Din_5_0[4]), .Sel(Dsel), .Clk(Clk), .Dout(out_4[4]));
  _1_bit_register u_1_bit_register_6 (.Din(Din_5_0[5]), .Sel(Dsel), .Clk(Clk), .Dout(out_4[5]));
endmodule

module _3_6_bit_register (
  input  Reg_en,
  input  [1:0] Wr,
  input  [5:0] Wrd,
  input  clk,
  input  [1:0] Ra,
  input  [1:0] Rb,
  output [5:0] out_7,
  output [5:0] out_8
);

  wire Reg0, Reg1, Reg2;
  wire [5:0] R0, R1, R2;

  Decoder #(.select(2)) decoder_1 (.out0(Reg0), .out1(Reg1), .out2(Reg2), .sel(Wr), .en(Reg_en));  // open: out3
  _6_bit_register u_6_bit_register_1 (.Din_5_0(Wrd), .Dsel(Reg0), .Clk(clk), .out_4(R0));
  _6_bit_register u_6_bit_register_2 (.Din_5_0(Wrd), .Dsel(Reg1), .Clk(clk), .out_4(R1));
  _6_bit_register u_6_bit_register_3 (.Din_5_0(Wrd), .Dsel(Reg2), .Clk(clk), .out_4(R2));
  Multiplexer #(.select(2), .width(6), .enable("false")) multiplexer_1 (
    .in0(R0), .in1(R1), .in2(R2), .out(out_7), .sel(Ra));  // open: in3
  Multiplexer #(.select(2), .width(6), .enable("false")) multiplexer_2 (
    .in0(R0), .in1(R1), .in2(R2), .out(out_8), .sel(Rb));  // open: in3
endmodule

module _1x1_SRAM (
  input  Read_Select_1,
  input  Read_Select_2,
  input  Write_Data,
  input  Write_Select,
  input  Clk,
  output Read_Data_1,
  output Read_Data_2
);

  wire d_ff_1_q, multiplexer_1_out;

  Multiplexer #(.enable("false")) multiplexer_1 (
    .in0(d_ff_1_q), .in1(Write_Data), .out(multiplexer_1_out), .sel(Write_Select));
  D_Flip_Flop d_ff_1 (.clk(Clk), .D(multiplexer_1_out), .Q(d_ff_1_q));  // open: Qn, preset, en, reset
  and and_1 (Read_Data_1, Read_Select_1, d_ff_1_q);
  and and_2 (Read_Data_2, Read_Select_2, d_ff_1_q);
endmodule

module _1x3_SRAM (
  input  Read_Select_1,
  input  Read_Select_2,
  input  Write_Select,
  input  [2:0] Write_Data,
  input  Clk,
  output [2:0] Read_Data_1,
  output [2:0] Read_Data_2
);

  _1x1_SRAM u_1x1_sram_1 (
    .Write_Data(Write_Data[0]), .Write_Select(Write_Select), .Clk(Clk), .Read_Data_1(Read_Data_1[0]),
    .Read_Data_2(Read_Data_2[0]), .Read_Select_1(Read_Select_1), .Read_Select_2(Read_Select_2));
  _1x1_SRAM u_1x1_sram_2 (
    .Write_Data(Write_Data[1]), .Write_Select(Write_Select), .Clk(Clk), .Read_Data_1(Read_Data_1[1]),
    .Read_Data_2(Read_Data_2[1]), .Read_Select_1(Read_Select_1), .Read_Select_2(Read_Select_2));
  _1x1_SRAM u_1x1_sram_3 (
    .Write_Data(Write_Data[2]), .Write_Select(Write_Select), .Clk(Clk), .Read_Data_1(Read_Data_1[2]),
    .Read_Data_2(Read_Data_2[2]), .Read_Select_1(Read_Select_1), .Read_Select_2(Read_Select_2));
endmodule

module _1x15_SRAM (
  input  Read_Select_1,
  input  Read_Select_2,
  input  Write_Select,
  input  Clk,
  input  [14:0] Write_data__14_0,
  output [14:0] Read_Data_1_14_0,
  output [14:0] Read_Data_2__14_0
);

  _1x3_SRAM u_1x3_sram_1 (
    .Read_Select_1(Read_Select_1), .Read_Select_2(Read_Select_2), .Write_Select(Write_Select),
    .Write_Data(Write_data__14_0[2:0]), .Clk(Clk), .Read_Data_1(Read_Data_1_14_0[2:0]),
    .Read_Data_2(Read_Data_2__14_0[2:0]));
  _1x3_SRAM u_1x3_sram_2 (
    .Read_Select_1(Read_Select_1), .Read_Select_2(Read_Select_2), .Write_Select(Write_Select),
    .Write_Data(Write_data__14_0[5:3]), .Clk(Clk), .Read_Data_1(Read_Data_1_14_0[5:3]),
    .Read_Data_2(Read_Data_2__14_0[5:3]));
  _1x3_SRAM u_1x3_sram_3 (
    .Read_Select_1(Read_Select_1), .Read_Select_2(Read_Select_2), .Write_Select(Write_Select),
    .Write_Data(Write_data__14_0[8:6]), .Clk(Clk), .Read_Data_1(Read_Data_1_14_0[8:6]),
    .Read_Data_2(Read_Data_2__14_0[8:6]));
  _1x3_SRAM u_1x3_sram_4 (
    .Read_Select_1(Read_Select_1), .Read_Select_2(Read_Select_2), .Write_Select(Write_Select),
    .Write_Data(Write_data__14_0[11:9]), .Clk(Clk), .Read_Data_1(Read_Data_1_14_0[11:9]),
    .Read_Data_2(Read_Data_2__14_0[11:9]));
  _1x3_SRAM u_1x3_sram_5 (
    .Read_Select_1(Read_Select_1), .Read_Select_2(Read_Select_2), .Write_Select(Write_Select),
    .Write_Data(Write_data__14_0[14:12]), .Clk(Clk), .Read_Data_1(Read_Data_1_14_0[14:12]),
    .Read_Data_2(Read_Data_2__14_0[14:12]));
endmodule

module _8x15_SRAM (
  input  [14:0] in_1,
  input  Write_Enable,
  input  [2:0] Write_Address_1_2_0,
  input  Read_Address_1_Enable,
  input  [2:0] Read_Address_1_2_0,
  input  Read_Address_2_Enable,
  input  [2:0] Read_Address_2_2_0,
  input  in_8,
  output [14:0] Read_data_1,
  output [14:0] Read_data_2
);

  wire R1_0, R1_1, R1_2, R1_3, R1_4, R1_5, R1_6, R1_7, R2_0, R2_1, R2_2, R2_3, R2_4, R2_5, R2_6, R2_7, W_0,
       W_1, W_2, W_3, W_4, W_5, W_6;
  wire [14:0] Rd1_0, Rd1_1, Rd1_2, Rd1_3, Rd1_4, Rd1_5, Rd1_6, Rd1_7, Rd2_0, Rd2_1, Rd2_2, Rd2_3, Rd2_4,
       Rd2_5, Rd2_6, Rd2_7;

  Decoder #(.select(3)) decoder_1 (
    .out0(W_0), .out1(W_1), .out2(W_2), .out3(W_3), .out4(W_4), .out5(W_5), .out6(W_6), .out7(R2_7),
    .sel(Write_Address_1_2_0), .en(Write_Enable));
  Decoder #(.select(3)) decoder_2 (
    .out0(R1_0), .out1(R1_1), .out2(R1_2), .out3(R1_3), .out4(R1_4), .out5(R1_5), .out6(R1_6), .out7(R1_7),
    .sel(Read_Address_1_2_0), .en(Read_Address_1_Enable));
  Decoder #(.select(3)) decoder_3 (
    .out0(R2_0), .out1(R2_1), .out2(R2_2), .out3(R2_3), .out4(R2_4), .out5(R2_5), .out6(R2_6), .out7(R2_7),
    .sel(Read_Address_2_2_0), .en(Read_Address_2_Enable));
  _1x15_SRAM u_1x15_sram_1 (
    .Read_Select_1(R1_0), .Read_Select_2(R2_0), .Write_Select(W_0), .Clk(in_8), .Write_data__14_0(in_1),
    .Read_Data_1_14_0(Rd1_0), .Read_Data_2__14_0(Rd2_0));
  _1x15_SRAM u_1x15_sram_2 (
    .Read_Select_1(R1_1), .Read_Select_2(R2_1), .Write_Select(W_1), .Clk(in_8), .Write_data__14_0(in_1),
    .Read_Data_1_14_0(Rd1_1), .Read_Data_2__14_0(Rd2_1));
  _1x15_SRAM u_1x15_sram_3 (
    .Read_Select_1(R1_2), .Read_Select_2(R2_2), .Write_Select(W_2), .Clk(in_8), .Write_data__14_0(in_1),
    .Read_Data_1_14_0(Rd1_2), .Read_Data_2__14_0(Rd2_2));
  _1x15_SRAM u_1x15_sram_4 (
    .Read_Select_1(R1_3), .Read_Select_2(R2_3), .Write_Select(W_3), .Clk(in_8), .Write_data__14_0(in_1),
    .Read_Data_1_14_0(Rd1_3), .Read_Data_2__14_0(Rd2_3));
  _1x15_SRAM u_1x15_sram_5 (
    .Read_Select_1(R1_4), .Read_Select_2(R2_4), .Write_Select(W_4), .Clk(in_8), .Write_data__14_0(in_1),
    .Read_Data_1_14_0(Rd1_4), .Read_Data_2__14_0(Rd2_4));
  _1x15_SRAM u_1x15_sram_6 (
    .Read_Select_1(R1_5), .Read_Select_2(R2_5), .Write_Select(W_5), .Clk(in_8), .Write_data__14_0(in_1),
    .Read_Data_1_14_0(Rd1_5), .Read_Data_2__14_0(Rd2_5));
  _1x15_SRAM u_1x15_sram_7 (
    .Read_Select_1(R1_6), .Read_Select_2(R2_6), .Write_Select(W_6), .Clk(in_8), .Write_data__14_0(in_1),
    .Read_Data_1_14_0(Rd1_6), .Read_Data_2__14_0(Rd2_6));
  _1x15_SRAM u_1x15_sram_8 (
    .Read_Select_1(R1_7), .Read_Select_2(R2_7), .Write_Select(R2_7), .Clk(in_8), .Write_data__14_0(in_1),
    .Read_Data_1_14_0(Rd1_7), .Read_Data_2__14_0(Rd2_7));
  assign Read_data_1 = Rd1_0 | Rd1_1 | Rd1_2 | Rd1_3 | Rd1_4 | Rd1_5 | Rd1_6 | Rd1_7;  // OR_Gate or_1, 15 bits wide
  assign Read_data_2 = Rd2_0 | Rd2_1 | Rd2_2 | Rd2_3 | Rd2_4 | Rd2_5 | Rd2_6 | Rd2_7;  // OR_Gate or_2, 15 bits wide

  // Other names for the same wires on the sheet: W_7 = R2_7
endmodule

module Control_Unit (
  input  [5:0] Opcode_5_0,
  input  ZF,
  input  SF,
  input  CF,
  output Imm_Sel,
  output REG_EN,
  output [3:0] Op_3_0,
  output Jmp_Reg_Sel,
  output Jmp_Sel
);

  wire and_1_out, and_2_out, CMP_out, Imm_2_out, JC_out, JE_out, JG_out, JGE_out, JL_out, JLE_out, Jmp_2_out,
       Jmp_3_out, JMP_out, JMP_REG_out, JNC_out, JNE_out, JNZ_out, JZ_out, not_1_out, or_1_out, or_2_out,
       or_3_out, or_4_out, or_5_out, Reg_out;

  and JMP (JMP_out, ~Opcode_5_0[0], ~Opcode_5_0[1], ~Opcode_5_0[2], ~Opcode_5_0[3]);  // AND_Gate
  and Imm (Imm_Sel, ~Opcode_5_0[5], Opcode_5_0[4]);  // AND_Gate
  and Jmp_2 (Jmp_2_out, Opcode_5_0[5], ~Opcode_5_0[4]);  // AND_Gate
  and Imm_2 (Imm_2_out, ~Opcode_5_0[5], Opcode_5_0[4]);  // AND_Gate
  and Reg (Reg_out, ~Opcode_5_0[5], ~Opcode_5_0[4]);  // AND_Gate
  not not_1 (not_1_out, Opcode_5_0[2]);
  and JE (JE_out, ~SF, ZF, Opcode_5_0[0], ~Opcode_5_0[1], ~Opcode_5_0[2], ~Opcode_5_0[3]);  // AND_Gate
  and CMP (CMP_out, Opcode_5_0[3], not_1_out, Opcode_5_0[1], Opcode_5_0[0]);
  and JNE (JNE_out, ~ZF, ~Opcode_5_0[0], Opcode_5_0[1], ~Opcode_5_0[2], ~Opcode_5_0[3]);  // AND_Gate
  and Jmp_3 (Jmp_3_out, Opcode_5_0[5], ~Opcode_5_0[4]);  // AND_Gate
  or or_1 (or_1_out, Imm_2_out, Reg_out);
  and and_1 (and_1_out, or_1_out, CMP_out);
  and JL (JL_out, SF, ~ZF, Opcode_5_0[0], Opcode_5_0[1], ~Opcode_5_0[2], ~Opcode_5_0[3]);  // AND_Gate
  or or_2 (or_2_out, SF, ZF);
  and JLE (JLE_out, or_2_out, ~Opcode_5_0[0], ~Opcode_5_0[1], Opcode_5_0[2], ~Opcode_5_0[3]);  // AND_Gate
  and JG (JG_out, ~SF, ~ZF, Opcode_5_0[0], ~Opcode_5_0[1], Opcode_5_0[2], ~Opcode_5_0[3]);  // AND_Gate
  or or_3 (or_3_out, JMP_out, JE_out, JNE_out, JL_out, JLE_out, JG_out, JGE_out, JC_out, JNC_out, JZ_out, JNZ_out);
  or or_4 (or_4_out, ~SF, ZF);  // OR_Gate
  and JGE (JGE_out, or_4_out, ~Opcode_5_0[0], Opcode_5_0[1], Opcode_5_0[2], ~Opcode_5_0[3]);  // AND_Gate
  and JC (JC_out, CF, Opcode_5_0[0], Opcode_5_0[1], Opcode_5_0[2], ~Opcode_5_0[3]);  // AND_Gate
  and JNC (JNC_out, ~CF, ~Opcode_5_0[0], ~Opcode_5_0[1], ~Opcode_5_0[2], Opcode_5_0[3]);  // AND_Gate
  and and_2 (and_2_out, or_3_out, Jmp_3_out);
  and JZ (JZ_out, ZF, Opcode_5_0[0], ~Opcode_5_0[1], ~Opcode_5_0[2], Opcode_5_0[3]);  // AND_Gate
  or or_5 (or_5_out, Jmp_2_out, and_1_out);
  not not_2 (REG_EN, or_5_out);
  and JNZ (JNZ_out, ~ZF, ~Opcode_5_0[0], Opcode_5_0[1], ~Opcode_5_0[2], Opcode_5_0[3]);  // AND_Gate
  and JMP_REG (JMP_REG_out, Opcode_5_0[0], Opcode_5_0[1], ~Opcode_5_0[2], Opcode_5_0[3]);  // AND_Gate
  and and_3 (Jmp_Reg_Sel, Jmp_3_out, JMP_REG_out);
  or or_6 (Jmp_Sel, Jmp_Reg_Sel, and_2_out);

  assign Op_3_0 = Opcode_5_0[3:0];
endmodule

module CPU (
);

  wire alu_1_cf, alu_1_sf, alu_1_zf;
  wire [5:0] alu_1_out_5, n3_6_bit_register_1_out_7;

  program_counter program_counter_1 ();  // open: I__2_0, Clock, O__2_0
  _8x15_SRAM u_8x15_sram_1 ();  // open: in_1, Write_Enable, Write_Address_1_2_0, Read_Address_1_Enable, Read_Address_1_2_0, Read_Address_2_Enable, Read_Address_2_2_0, in_8, Read_data_1, Read_data_2
  _3_6_bit_register u_3_6_bit_register_1 (
    .Wrd(alu_1_out_5), .out_7(n3_6_bit_register_1_out_7));  // open: Reg_en, Wr, clk, Ra, Rb, out_8
  Flag_register flag_register_1 (.CF(alu_1_cf), .SF(alu_1_sf), .ZF(alu_1_zf));  // open: Clock, CF_2, SF_2, ZF_2
  Control_Unit control_unit_1 ();  // open: Opcode_5_0, ZF, SF, CF, Imm_Sel, REG_EN, Op_3_0, Jmp_Reg_Sel, Jmp_Sel
  ALU alu_1 (
    .A_5_0(n3_6_bit_register_1_out_7), .out_5(alu_1_out_5), .SF(alu_1_sf), .CF(alu_1_cf), .ZF(alu_1_zf));  // open: B_5_0, Shift_2_0, OP
endmodule

module program_counter (
  input  [2:0] I__2_0,
  input  Clock,
  output [2:0] O__2_0
);

  D_Flip_Flop d_ff_1 (.clk(Clock), .D(I__2_0[0]), .Q(O__2_0[0]));  // open: Qn, preset, en, reset
  D_Flip_Flop d_ff_2 (.clk(Clock), .D(I__2_0[1]), .Q(O__2_0[1]));  // open: Qn, preset, en, reset
  D_Flip_Flop d_ff_3 (.clk(Clock), .D(I__2_0[2]), .Q(O__2_0[2]));  // open: Qn, preset, en, reset
endmodule

module Flag_register (
  input  CF,
  input  SF,
  input  ZF,
  input  Clock,
  output CF_2,
  output SF_2,
  output ZF_2
);

  _1_bit_register u_1_bit_register_1 (.Din(CF), .Sel(1'b1), .Clk(Clock), .Dout(CF_2));
  _1_bit_register u_1_bit_register_2 (.Din(SF), .Sel(1'b1), .Clk(Clock), .Dout(SF_2));
  _1_bit_register u_1_bit_register_3 (.Din(ZF), .Sel(1'b1), .Clk(Clock), .Dout(ZF_2));
endmodule

module ROM (
  input  Clock,
  input  PC_Enable,
  output [2:0] Physical_Address,
  output [14:0] Data,
  output Write_Enable,
  output PC_Clock
);

  Counter #(.width(3), .max('h7), .ongoal("stay")) counter_1 (
    .Q(Physical_Address), .clk(Clock));  // open: load, D, count, carry, clr
  not not_1 (Write_Enable, PC_Enable);
  and and_1 (PC_Clock, Clock, PC_Enable);
  ROM_part #(.addrWidth(3), .dataWidth(15)) rom_1 (.addr(Physical_Address), .data(Data));  // open: sel

  // Notes on the sheet:
  //   contents of rom_1 (hex, n*v repeats v):
  //   a40 9b0 5621 55b0 2e30 1840 5581 41
endmodule
